# Fritzing sketch min mobil rc (saved by Fritzing 0.9.3b)
breadboards: 1

parts:
  A1 = MX1508
  M1 = DOIT Esp32 DevKit v1 (30 pins long, 11 pins width) [part_number=ESP32S-PIN30]
  M2 = DC Motor
  M3 = DC Motor

nets:
  N1: A1.Pin_1, M1.VIN
  N2: A1.Pin_2, M1.GND
  N3: A1.Pin_3, M1.D19
  N4: A1.Pin_4, M1.D18
  N5: A1.Pin_5, M1.TX2
  N6: A1.Pin_6, M1.RX2
  N7: A1.Pin_7, M3.pin_2
  N8: A1.Pin_8, M3.pin_1
  N9: A1.Pin_9, M2.pin_2
  N10: A1.Pin_10, M2.pin_1

custom parts:
  MX1508: MX1508 DC Motor Driver is a low-cost motor driver module that can control DC stepper motors of current rating up to 2A.
  DOIT Esp32 DevKit v1 (30 pins long, 11 pins width): The DOIT Esp32 DevKit v1 is one of the development board created by DOIT to evaluate the ESP-WROOM-32 module. It is based on the ESP32 microcontroller that boasts Wifi, Bluetooth, Ethernet and Low Power support all in a single chip. (vanepp) made breadboard work, adjusted pin numbering and labels and reduced size of schematic and cleaned up pcb. This chip is 30pins long (2 x15) and 11 pins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
